# Fritzing sketch PROYECTO ELECTRÓNICO LASER NAVIGATION SYSTEM (saved by Fritzing 0.9.3b)
circuit board: 8.46667cm x 5.64444cm

parts:
  Q1 = LTR-301 [package=ltr-301]
  LED1 = LEDs [package=led10mm]
  R1 = Resistor [tolerance=±5% resistance=220 package=THT]
  PS1 = prefix0000 [part_number=S-350-60]
  M1 = DC Motor
  S3 = H-Bridge with L298N
  Part1 = node32s
  Mod1 = KY-024 Linear Hall Magnetic Sensor Module [package="Breakout board"]
  R2 = Resistor [tolerance=±5% resistance=220 package="2010 [SMD]"]
  LED3 = RGB LED (com. cathode, rgb) [package="5 mm [THT]"]
  R3 = Resistor [tolerance=±5% resistance=220 package="0402 [SMD]"]
  R4 = Resistor [tolerance=±5% resistance=220 package="0402 [SMD]"]
  R5 = Resistor [tolerance=±5% resistance=220 package="0402 [SMD]"]

nets (from the schematic view):
  N1: Q1.C, Part1.3.3V
  N2: Q1.E, Part1.IO13, R2.Pin_1
  N3: LED1.C, R1.Pin_1
  5V: LED1.A, S3.5V, Part1.5V, Mod1.+
  GND: R1.Pin_0, PS1.connector6, S3.GND, Part1.GND, Mod1.G, R2.Pin_0, LED3.common_cathode
  N4: PS1.connector2, S3.12V
  N5: M1.pin_2, S3.M1-02, S3.M2-01, S3.M2-02, S3.ENA-5V, S3.ENB-5V
  N6: S3.ENB, Part1.IO16
  N7: Part1.IO36, R3.Pin_1
  N8: Part1.IO34, R5.Pin_1
  N9: Part1.IO35, R4.Pin_1
  N10: Part1.IO10, Mod1.D0
  N11: LED3.red_anode, R5.Pin_0
  N12: LED3.green_anode, R4.Pin_0
  N13: LED3.blue_anode, R3.Pin_0

custom parts:
  H-Bridge with L298N: h-bridge
  KY-024 Linear Hall Magnetic Sensor Module: KY-024 Linear Hall Magnetic Sensor Module reacts iin the presence of a magnetic field.
